# Fritzing sketch Programming_ESP-01_rev2 (saved by Fritzing 0.9.3b)
circuit board: 8.46667cm x 5.64444cm
breadboards: 1

parts:
  JACK1 = 2.1mm Barrel Jack with Terminal Block [part_number="7-12V DC PSU, inline switch"]
  U2 = Voltage Regulator - 3.3V [part_number=UA78M33C package="TO220 [THT]"]
  U1 = ESP8266 WiFi Module [part_number=ESP-01]
  RESET = Momentary Switch [package=ksa_sealed_tac_switch]
  FLASH = Momentary Switch [package=ksa_sealed_tac_switch]
  R1 = Resistor [tolerance=±5% resistance=10k package=THT]
  C1 = Ceramic Capacitor [capacitance=0.1µF package="100 mil [THT, multilayer]"]
  C3 = Ceramic Capacitor [capacitance=0.1µF part_number="3 ∥ 0.1µF" package="100 mil [THT, multilayer]"]
  C4 = Electrolytic Capacitor [capacitance=100μF package="0807 [SMD, electrolytic]"]
  USBTTL1 = USB TTL Serial Cable [part_number=FT-232R-3V3]
  R2 = Resistor [tolerance=±5% resistance=10k package=THT]
  LED1 = LED - 3mm [color="Blue (470nm)" package="3 mm [THT]"]
  R3 = Resistor [tolerance=±5% resistance=47 package=THT]

nets:
  N1: JACK1.POS, U2.input_voltage, C3.0
  GND: JACK1.NEG, U2.GND, U1.GND, RESET.3, FLASH.3, C1.0, C3.1, C4.-, USBTTL1.GND, R3.Pin_0
  N2: U2.output_voltage, U1.VCC, R1.Pin_0, C1.1, C4.+, R2.Pin_0, LED1.anode
  N3: U1.RXD, USBTTL1.TX
  N4: U1.GPIO_0, FLASH.2
  N5: U1.GPIO_16, RESET.2, R2.Pin_1
  N6: U1.CH_PD, R1.Pin_1
  N7: U1.TXD, USBTTL1.RX
  N8: LED1.cathode, R3.Pin_1

custom parts:
  ESP8266 WiFi Module: Generic WiFi Module based on the ESP8266 with onboard PCB antenna and UART communications
